# Fritzing sketch arduino_CVToMIDI Sketch (saved by Fritzing 0.9.4)
circuit board: 8.46667cm x 5.64444cm
breadboards: 1

parts:
  Bauteil1 = Arduino Nano (Rev3.0)
  U1 = MIDI_CONN_FEMALE_SUPPORT [package=din_5_female_support]
  R1 = Trimmer Potentiometer [maximum_resistance=10kΩ package=THT]
  OLED_I2C1 = OLED 128x64 I2C Monochrome Display
  TRS2 = Audio Jack (TRRS) 3.5mm [part_number="LUMBERG JEITA RC-5325A" package="RC-5325A [SMD]"]
  R2 = Trimmer Potentiometer [maximum_resistance=10kΩ package=THT]
  R6 = Resistor [tolerance=±5% resistance=220 package=THT]
  R5 = Resistor [tolerance=±5% resistance=220 package=THT]
  TRS1 = Audio Jack (TRRS) 3.5mm [part_number="LUMBERG JEITA RC-5325A" package="RC-5325A [SMD]"]

nets:
  N1: Bauteil1.D1/TX, R5.Pin_0
  GND: Bauteil1.GND, U1.NC1, R1.leg1, OLED_I2C1.GND, TRS2.SLEEVE, R2.leg1, TRS1.SLEEVE
  5V: Bauteil1.5V, OLED_I2C1.VDD, R6.Pin_0
  N2: Bauteil1.A5, OLED_I2C1.SCK
  N3: Bauteil1.A4, OLED_I2C1.SDA
  N4: Bauteil1.A1, R2.wiper
  N5: Bauteil1.A0, R1.wiper
  N6: U1.MIDI_IN, R5.Pin_1
  N7: U1.MIDI_OUT, R6.Pin_1
  N8: R1.leg2, TRS1.TIP
  N9: TRS2.TIP, R2.leg2
